# Fritzing sketch tape_following_circuitry (saved by Fritzing 0.9.2b)
breadboards: 2

parts:
  Part1 = Arduino Motor Shield (Rev3)  # not connected
  Q3 = PHOTOTRANSISTOR REFLECTIVE OBJECT SENSOR [package=qrb1114-side]
  Q4 = PHOTOTRANSISTOR REFLECTIVE OBJECT SENSOR [package=qrb1114-side]
  R5 = Resistor [tolerance=±5% resistance=220 package="2010 [SMD]"]
  R6 = Resistor [tolerance=±5% resistance=220 package="2010 [SMD]"]
  R7 = Resistor [tolerance=±5% resistance=10k package="2010 [SMD]"]
  R8 = Resistor [tolerance=±5% resistance=10k package="2010 [SMD]"]

nets:
  N1: Q3.A, R8.Pin_0
  N2: Q3.C, R5.Pin_0
  N3: Q3.E, Q3.K
  N4: Q4.A, R7.Pin_0
  N5: Q4.C, R6.Pin_0
  N6: Q4.E, Q4.K, R5.Pin_1, R6.Pin_1, R7.Pin_1, R8.Pin_1

notes:
  TO TAPE
  TO HUB
  HUB
  TAPE
